// Logisim project prob2.circ as structural Verilog: 1 circuit, main circuit main
module main (
  input  ER,
  input  DSBF,
  input  DC,
  input  DLC,
  input  KIC,
  input  DOS,
  input  BP,
  input  CM,
  output BELL,
  output DLA,
  output BA
);

  wire not_1_out, not_2_out, not_3_out, or_1_out, or_2_out;

  not not_1 (not_1_out, DSBF);
  not not_2 (not_2_out, DC);
  not not_3 (not_3_out, KIC);
  and and_1 (BA, BP, CM);
  or or_1 (or_1_out, not_1_out, not_2_out);
  or or_2 (or_2_out, not_3_out, DOS);
  and and_2 (BELL, ER, or_1_out);
  and and_3 (DLA, DLC, or_2_out);
endmodule
