// Logisim project ex4.circ as structural Verilog: 7 circuits, main circuit main
module main (
  input  in_1
);
endmodule

module full_adder (
  input  cin,
  input  a,
  input  b,
  output out,
  output cout
);

  wire and_1_out, and_2_out, xor_1_out;

  xor xor_1 (xor_1_out, a, b);
  xor xor_2 (out, cin, xor_1_out);
  and and_1 (and_1_out, xor_1_out, cin);
  and and_2 (and_2_out, a, b);
  xor xor_3 (cout, and_1_out, and_2_out);
endmodule

module _8bit_adder (
  input  [7:0] a,
  input  [7:0] b,
  output [7:0] out_3,
  output overflow
);

  wire full_adder_1_cout, full_adder_2_cout, full_adder_3_cout, full_adder_4_cout, full_adder_5_cout,
       full_adder_6_cout, full_adder_7_cout, xnor_1_out, xor_1_out;

  full_adder full_adder_1 (.cin(full_adder_2_cout), .a(a[1]), .b(b[1]), .out(out_3[1]), .cout(full_adder_1_cout));
  full_adder full_adder_2 (.cin(1'b0), .a(a[0]), .b(b[0]), .out(out_3[0]), .cout(full_adder_2_cout));
  xnor xnor_1 (xnor_1_out, b[7], a[7]);
  full_adder full_adder_3 (.cin(full_adder_1_cout), .a(a[2]), .b(b[2]), .out(out_3[2]), .cout(full_adder_3_cout));
  xor xor_1 (xor_1_out, b[7], out_3[7]);
  full_adder full_adder_4 (.cin(full_adder_3_cout), .a(a[3]), .b(b[3]), .out(out_3[3]), .cout(full_adder_4_cout));
  full_adder full_adder_5 (.cin(full_adder_4_cout), .a(a[4]), .b(b[4]), .out(out_3[4]), .cout(full_adder_5_cout));
  and and_1 (overflow, xnor_1_out, xor_1_out);
  full_adder full_adder_6 (.cin(full_adder_5_cout), .a(a[5]), .b(b[5]), .out(out_3[5]), .cout(full_adder_6_cout));
  full_adder full_adder_7 (.cin(full_adder_6_cout), .a(a[6]), .b(b[6]), .out(out_3[6]), .cout(full_adder_7_cout));
  full_adder full_adder_8 (.cin(full_adder_7_cout), .a(a[7]), .b(b[7]), .out(out_3[7]));  // open: cout
endmodule

module _8bits_subtractor (
  input  [7:0] A,
  input  [7:0] B,
  output [7:0] out_3
);

  wire [7:0] inverter_1_out_2;

  inverter inverter_1 (.A(B), .out_2(inverter_1_out_2));
  _8bit_adder u_8bit_adder_1 (.a(A), .b(inverter_1_out_2), .out_3(out_3));  // open: overflow
endmodule

module inverter (
  input  [7:0] A,
  output [7:0] out_2
);

  wire [7:0] not_1_out;

  not not_1 (not_1_out[0], A[0]);
  not not_2 (not_1_out[1], A[1]);
  not not_3 (not_1_out[2], A[2]);
  not not_4 (not_1_out[3], A[3]);
  not not_5 (not_1_out[4], A[4]);
  not not_6 (not_1_out[5], A[5]);
  not not_7 (not_1_out[6], A[6]);
  not not_8 (not_1_out[7], A[7]);
  _8bit_adder u_8bit_adder_1 (.a(not_1_out), .b(8'h1), .out_3(out_2));  // open: overflow
endmodule

module half_mag_comp (
  input  a,
  input  b,
  input  gt,
  input  eq,
  input  lt,
  output gt_o,
  output eq_o,
  output lt_o
);

  wire and_1_out, and_2_out, xnor_1_out;

  and and_1 (and_1_out, a, eq, ~b);  // AND_Gate
  xnor xnor_1 (xnor_1_out, b, a);
  and and_2 (and_2_out, b, eq, ~a);  // AND_Gate
  or or_1 (gt_o, and_1_out, gt);
  and and_3 (eq_o, xnor_1_out, eq);
  or or_2 (lt_o, and_2_out, lt);
endmodule

module mag_comp (
  input  [7:0] a,
  input  [7:0] b,
  output out_3,
  output out_4,
  output out_5
);

  wire half_mag_comp_1_eq_o, half_mag_comp_1_gt_o, half_mag_comp_1_lt_o, half_mag_comp_2_eq_o,
       half_mag_comp_2_gt_o, half_mag_comp_2_lt_o, half_mag_comp_3_eq_o, half_mag_comp_3_gt_o,
       half_mag_comp_3_lt_o, half_mag_comp_4_eq_o, half_mag_comp_4_gt_o, half_mag_comp_4_lt_o,
       half_mag_comp_5_eq_o, half_mag_comp_5_gt_o, half_mag_comp_5_lt_o, half_mag_comp_6_eq_o,
       half_mag_comp_6_gt_o, half_mag_comp_6_lt_o, half_mag_comp_7_eq_o, half_mag_comp_7_gt_o,
       half_mag_comp_7_lt_o;

  half_mag_comp half_mag_comp_1 (
    .a(a[7]), .b(b[7]), .gt(1'b0), .eq(1'b1), .lt(1'b0), .gt_o(half_mag_comp_1_gt_o),
    .eq_o(half_mag_comp_1_eq_o), .lt_o(half_mag_comp_1_lt_o));
  half_mag_comp half_mag_comp_2 (
    .a(a[6]), .b(b[6]), .gt(half_mag_comp_1_gt_o), .eq(half_mag_comp_1_eq_o), .lt(half_mag_comp_1_lt_o),
    .gt_o(half_mag_comp_2_gt_o), .eq_o(half_mag_comp_2_eq_o), .lt_o(half_mag_comp_2_lt_o));
  half_mag_comp half_mag_comp_3 (
    .a(a[5]), .b(b[5]), .gt(half_mag_comp_2_gt_o), .eq(half_mag_comp_2_eq_o), .lt(half_mag_comp_2_lt_o),
    .gt_o(half_mag_comp_3_gt_o), .eq_o(half_mag_comp_3_eq_o), .lt_o(half_mag_comp_3_lt_o));
  half_mag_comp half_mag_comp_4 (
    .a(a[4]), .b(b[4]), .gt(half_mag_comp_3_gt_o), .eq(half_mag_comp_3_eq_o), .lt(half_mag_comp_3_lt_o),
    .gt_o(half_mag_comp_4_gt_o), .eq_o(half_mag_comp_4_eq_o), .lt_o(half_mag_comp_4_lt_o));
  half_mag_comp half_mag_comp_5 (
    .a(a[3]), .b(b[3]), .gt(half_mag_comp_4_gt_o), .eq(half_mag_comp_4_eq_o), .lt(half_mag_comp_4_lt_o),
    .gt_o(half_mag_comp_5_gt_o), .eq_o(half_mag_comp_5_eq_o), .lt_o(half_mag_comp_5_lt_o));
  half_mag_comp half_mag_comp_6 (
    .a(a[2]), .b(b[2]), .gt(half_mag_comp_5_gt_o), .eq(half_mag_comp_5_eq_o), .lt(half_mag_comp_5_lt_o),
    .gt_o(half_mag_comp_6_gt_o), .eq_o(half_mag_comp_6_eq_o), .lt_o(half_mag_comp_6_lt_o));
  half_mag_comp half_mag_comp_7 (
    .a(a[1]), .b(b[1]), .gt(half_mag_comp_6_gt_o), .eq(half_mag_comp_6_eq_o), .lt(half_mag_comp_6_lt_o),
    .gt_o(half_mag_comp_7_gt_o), .eq_o(half_mag_comp_7_eq_o), .lt_o(half_mag_comp_7_lt_o));
  half_mag_comp half_mag_comp_8 (
    .a(a[0]), .b(b[0]), .gt(half_mag_comp_7_gt_o), .eq(half_mag_comp_7_eq_o), .lt(half_mag_comp_7_lt_o),
    .gt_o(out_3), .eq_o(out_4), .lt_o(out_5));
endmodule
